// Logisim project 104418019_2.circ as structural Verilog: 2 circuits, main circuit main
module main (
  output halt,
  output [11:0] C,
  output [6:0] O1,
  output [6:0] O2,
  output [6:0] O3
);

  wire clock_1_out;

  Clock clock_1 (.out(clock_1_out));
  Counter #(.width(12), .max('hfff)) counter_1 (
    .clk(clock_1_out), .carry(halt), .Q(C));  // open: clr, load, up, count, D
  SSD ssd_1 (.I(C[11:8]), .O(O1));
  _7_Segment_Display u_7_segment_display_1 (
    .g(O1[3]), .f(O1[2]), .a(O1[1]), .b(O1[0]), .e(O1[4]), .d(O1[5]), .c(O1[6]));  // open: dp
  _7_Segment_Display u_7_segment_display_2 (
    .g(O2[3]), .f(O2[2]), .a(O2[1]), .b(O2[0]), .e(O2[4]), .d(O2[5]), .c(O2[6]));  // open: dp
  SSD ssd_2 (.I(C[7:4]), .O(O2));
  SSD ssd_3 (.I(C[3:0]), .O(O3));
  _7_Segment_Display u_7_segment_display_3 (
    .g(O3[3]), .f(O3[2]), .a(O3[1]), .b(O3[0]), .e(O3[4]), .d(O3[5]), .c(O3[6]));  // open: dp

  // Other names for the same wires on the sheet: D0[3:0] = C[3:0]; D1[3:0] = C[7:4]; D2[3:0] = C[11:8]

  // Notes on the sheet:
  //   Attention, votre version de Logisim
  //   ne contient pas de tracker. Si vous
  //   enregistrez votre projet, toutes les
  //   informations du tracker seront
  //   définitivement effacées.
endmodule

module SSD (
  input  [3:0] I,
  output [6:0] O
);

  ROM #(.addrWidth(4), .dataWidth(7)) rom_1 (.addr(I), .data(O));

  // Notes on the sheet:
  //   Attention, votre version de Logisim
  //   ne contient pas de tracker. Si vous
  //   enregistrez votre projet, toutes les
  //   informations du tracker seront
  //   définitivement effacées.
  //   contents of rom_1 (hex, n*v repeats v):
  //   77 41 3b 6b 4d 6e 7e 43 7f 6f 5f 7c 38 79 3e 1e
endmodule
