// Logisim project 104418019_3a.circ as structural Verilog: 2 circuits, main circuit main
module main (
  output halt
);

  wire clock_1_out;
  wire [5:0] counter_1_q;
  wire [6:0] bit_extender_1_out;
  wire [7:0] mycircuit_1_d;

  Clock clock_1 (.out(clock_1_out));
  Counter #(.width(6), .max('h3f)) counter_1 (
    .clk(clock_1_out), .carry(halt), .Q(counter_1_q));  // open: clr, load, up, count, D
  // Probe on counter_1_q
  TTY tty_1 (.data(bit_extender_1_out), .clk(clock_1_out));  // open: we, clr
  mycircuit mycircuit_1 (.A(counter_1_q), .D(mycircuit_1_d));
  // Probe on bit_extender_1_out
  Bit_Extender #(.out_width(7), .\type ("zero")) bit_extender_1 (.in(mycircuit_1_d), .out(bit_extender_1_out));

  // Notes on the sheet:
  //   Attention, votre version de Logisim
  //   ne contient pas de tracker. Si vous
  //   enregistrez votre projet, toutes les
  //   informations du tracker seront
  //   définitivement effacées.
endmodule

module mycircuit (
  input  [5:0] A,
  output [7:0] D
);

  wire and_1_out, and_2_out, and_3_out, and_4_out, not_1_out, not_2_out, not_3_out, not_4_out;
  wire [7:0] ROM0_data, ROM1_data, ROM2_data, ROM3_data;

  not not_1 (not_1_out, A[5]);
  not not_2 (not_2_out, A[4]);
  not not_3 (not_3_out, A[5]);
  ROM #(.addrWidth(4)) ROM0 (.addr(A[3:0]), .data(ROM0_data));
  and and_1 (and_1_out, not_1_out, not_2_out);
  ROM #(.addrWidth(4)) ROM1 (.addr(A[3:0]), .data(ROM1_data));
  and and_2 (and_2_out, A[4], A[5]);
  ROM #(.addrWidth(4)) ROM2 (.addr(A[3:0]), .data(ROM2_data));
  and and_3 (and_3_out, A[4], not_3_out);
  ROM #(.addrWidth(4)) ROM3 (.addr(A[3:0]), .data(ROM3_data));
  not not_4 (not_4_out, A[4]);
  and and_4 (and_4_out, not_4_out, A[5]);
  assign D = and_4_out ? ROM0_data : 8'bz;  // Controlled_Buffer controlled_buffer_1
  assign D = and_1_out ? ROM1_data : 8'bz;  // Controlled_Buffer controlled_buffer_2
  assign D = and_2_out ? ROM2_data : 8'bz;  // Controlled_Buffer controlled_buffer_3
  assign D = and_3_out ? ROM3_data : 8'bz;  // Controlled_Buffer controlled_buffer_4

  // Other names for the same wires on the sheet: pos[3:0] = A[3:0]

  // Notes on the sheet:
  //   Attention, votre version de Logisim
  //   ne contient pas de tracker. Si vous
  //   enregistrez votre projet, toutes les
  //   informations du tracker seront
  //   définitivement effacées.
  //   contents of ROM0 (hex, n*v repeats v):
  //   72 65 73 74 20 6f 66 20 74 68 65 20 77 6f 72 6c
  //   contents of ROM1 (hex, n*v repeats v):
  //   41 20 72 65 61 6c 20 66 72 69 65 6e 64 20 77 61
  //   contents of ROM2 (hex, n*v repeats v):
  //   64 20 77 61 6c 6b 73 20 6f 75 74 2e a
  //   contents of ROM3 (hex, n*v repeats v):
  //   6c 6b 73 20 69 6e 20 77 68 65 6e 20 74 68 65 20
endmodule
