// Logisim project 104418019_3b.circ as structural Verilog: 2 circuits, main circuit main
module main (
  output halt
);

  wire clock_1_out;
  wire [5:0] counter_1_q;
  wire [6:0] bit_extender_1_out;
  wire [7:0] mycircuit_1_d;

  Clock clock_1 (.out(clock_1_out));
  Counter #(.width(6), .max('h3f)) counter_1 (
    .clk(clock_1_out), .carry(halt), .Q(counter_1_q));  // open: clr, load, up, count, D
  // Probe on counter_1_q
  TTY tty_1 (.data(bit_extender_1_out), .clk(clock_1_out));  // open: we, clr
  mycircuit mycircuit_1 (.A(counter_1_q), .D(mycircuit_1_d));
  // Probe on bit_extender_1_out
  Bit_Extender #(.out_width(7), .\type ("zero")) bit_extender_1 (.in(mycircuit_1_d), .out(bit_extender_1_out));

  // Notes on the sheet:
  //   Attention, votre version de Logisim
  //   ne contient pas de tracker. Si vous
  //   enregistrez votre projet, toutes les
  //   informations du tracker seront
  //   définitivement effacées.
endmodule

module mycircuit (
  input  [5:0] A,
  output [7:0] D
);

  wire and_1_out, and_2_out, and_3_out, and_4_out, and_5_out, and_6_out, and_7_out, and_8_out, not_1_out,
       not_2_out, not_3_out, not_4_out, not_5_out, not_6_out, not_7_out, not_8_out, not_9_out, not_10_out,
       not_11_out, not_12_out;
  wire [7:0] ROM0_data, ROM1_data, ROM2_data, ROM3_data, ROM4_data, ROM5_data, ROM6_data, ROM7_data;

  not not_1 (not_1_out, A[4]);
  and and_1 (and_1_out, not_1_out, not_2_out, not_3_out);
  not not_2 (not_2_out, A[3]);
  not not_3 (not_3_out, A[5]);
  and and_2 (and_2_out, A[4], not_4_out, not_5_out);
  not not_4 (not_4_out, A[3]);
  not not_5 (not_5_out, A[5]);
  not not_6 (not_6_out, A[4]);
  not not_7 (not_7_out, A[3]);
  and and_3 (and_3_out, not_6_out, not_7_out, A[5]);
  not not_8 (not_8_out, A[3]);
  and and_4 (and_4_out, A[4], not_8_out, A[5]);
  ROM #(.addrWidth(3)) ROM3 (.addr(A[2:0]), .data(ROM3_data));
  ROM #(.addrWidth(3)) ROM0 (.addr(A[2:0]), .data(ROM0_data));
  ROM #(.addrWidth(3)) ROM1 (.addr(A[2:0]), .data(ROM1_data));
  ROM #(.addrWidth(3)) ROM2 (.addr(A[2:0]), .data(ROM2_data));
  assign D = and_1_out ? ROM3_data : 8'bz;  // Controlled_Buffer controlled_buffer_1
  assign D = and_2_out ? ROM0_data : 8'bz;  // Controlled_Buffer controlled_buffer_2
  assign D = and_3_out ? ROM1_data : 8'bz;  // Controlled_Buffer controlled_buffer_3
  assign D = and_4_out ? ROM2_data : 8'bz;  // Controlled_Buffer controlled_buffer_4
  not not_9 (not_9_out, A[5]);
  not not_10 (not_10_out, A[4]);
  not not_11 (not_11_out, A[4]);
  and and_5 (and_5_out, not_11_out, A[3], not_12_out);
  not not_12 (not_12_out, A[5]);
  and and_6 (and_6_out, A[4], A[3], not_9_out);
  and and_7 (and_7_out, not_10_out, A[3], A[5]);
  and and_8 (and_8_out, A[4], A[3], A[5]);
  ROM #(.addrWidth(3)) ROM7 (.addr(A[2:0]), .data(ROM7_data));
  ROM #(.addrWidth(3)) ROM5 (.addr(A[2:0]), .data(ROM5_data));
  ROM #(.addrWidth(3)) ROM4 (.addr(A[2:0]), .data(ROM4_data));
  ROM #(.addrWidth(3)) ROM6 (.addr(A[2:0]), .data(ROM6_data));
  assign D = and_5_out ? ROM7_data : 8'bz;  // Controlled_Buffer controlled_buffer_5
  assign D = and_6_out ? ROM5_data : 8'bz;  // Controlled_Buffer controlled_buffer_6
  assign D = and_7_out ? ROM4_data : 8'bz;  // Controlled_Buffer controlled_buffer_7
  assign D = and_8_out ? ROM6_data : 8'bz;  // Controlled_Buffer controlled_buffer_8

  // Other names for the same wires on the sheet: pos[2:0] = A[2:0]

  // Notes on the sheet:
  //   Attention, votre version de Logisim
  //   ne contient pas de tracker. Si vous
  //   enregistrez votre projet, toutes les
  //   informations du tracker seront
  //   définitivement effacées.
  //   contents of ROM3 (hex, n*v repeats v):
  //   57 68 65 6e 65 76 65 72
  //   contents of ROM0 (hex, n*v repeats v):
  //   61 67 72 65 65 20 77 69
  //   contents of ROM1 (hex, n*v repeats v):
  //   61 6c 77 61 79 73 20 66
  //   contents of ROM2 (hex, n*v repeats v):
  //   73 74 20 62 65 20 77 72
  //   contents of ROM7 (hex, n*v repeats v):
  //   20 70 65 6f 70 6c 65 20
  //   contents of ROM5 (hex, n*v repeats v):
  //   74 68 20 6d 65 20 49 20
  //   contents of ROM4 (hex, n*v repeats v):
  //   65 65 6c 20 49 20 6d 75
  //   contents of ROM6 (hex, n*v repeats v):
  //   6f 6e 67 2e a
endmodule
