// Logisim project 104418019_3c.circ as structural Verilog: 2 circuits, main circuit main
module main (
  output halt
);

  wire clk;
  wire [5:0] counter_1_q;
  wire [6:0] bit_extender_1_out;
  wire [7:0] mycircuit_1_d;

  Clock clock_1 (.out(clk));
  Counter #(.width(6), .max('h3f)) counter_1 (
    .clk(clk), .carry(halt), .Q(counter_1_q));  // open: clr, load, up, count, D
  // Probe on counter_1_q
  TTY tty_1 (.data(bit_extender_1_out), .clk(clk));  // open: we, clr
  mycircuit mycircuit_1 (.A(counter_1_q), .D(mycircuit_1_d));
  // Probe on bit_extender_1_out
  Bit_Extender #(.out_width(7), .\type ("zero")) bit_extender_1 (.in(mycircuit_1_d), .out(bit_extender_1_out));

  // Notes on the sheet:
  //   Attention, votre version de Logisim
  //   ne contient pas de tracker. Si vous
  //   enregistrez votre projet, toutes les
  //   informations du tracker seront
  //   définitivement effacées.
endmodule

module mycircuit (
  input  [5:0] A,
  output [7:0] D
);

  wire eighth, fifth, first, fourth, not_1_out, not_2_out, not_3_out, second, seventh, sixth, third;
  wire [3:0] ROM0_data, ROM1_data, ROM2_data, ROM3_data, ROM4_data, ROM5_data, ROM6_data, ROM7_data,
       ROM8_data, ROM9_data, ROMA_data, ROMB_data, ROMC_data, ROMD_data, ROME_data, ROMF_data;

  not not_1 (not_1_out, A[5]);
  not not_2 (not_2_out, A[4]);
  not not_3 (not_3_out, A[3]);
  and and_1 (first, not_3_out, not_2_out, not_1_out);
  and and_2 (second, A[3], not_2_out, not_1_out);
  and and_3 (third, not_3_out, A[4], not_1_out);
  and and_4 (fourth, A[3], A[4], not_1_out);
  and and_5 (fifth, not_3_out, not_2_out, A[5]);
  and and_6 (sixth, A[3], not_2_out, A[5]);
  and and_7 (seventh, not_3_out, A[4], A[5]);
  and and_8 (eighth, A[3], A[4], A[5]);
  ROM #(.addrWidth(3), .dataWidth(4)) ROM9 (.addr(A[2:0]), .data(ROM9_data));
  ROM #(.addrWidth(3), .dataWidth(4)) ROM0 (.addr(A[2:0]), .data(ROM0_data));
  ROM #(.addrWidth(3), .dataWidth(4)) ROM7 (.addr(A[2:0]), .data(ROM7_data));
  ROM #(.addrWidth(3), .dataWidth(4)) ROM1 (.addr(A[2:0]), .data(ROM1_data));
  ROM #(.addrWidth(3), .dataWidth(4)) ROMD (.addr(A[2:0]), .data(ROMD_data));
  ROM #(.addrWidth(3), .dataWidth(4)) ROM3 (.addr(A[2:0]), .data(ROM3_data));
  ROM #(.addrWidth(3), .dataWidth(4)) ROM5 (.addr(A[2:0]), .data(ROM5_data));
  ROM #(.addrWidth(3), .dataWidth(4)) ROM2 (.addr(A[2:0]), .data(ROM2_data));
  ROM #(.addrWidth(3), .dataWidth(4)) ROMA (.addr(A[2:0]), .data(ROMA_data));
  ROM #(.addrWidth(3), .dataWidth(4)) ROMF (.addr(A[2:0]), .data(ROMF_data));
  ROM #(.addrWidth(3), .dataWidth(4)) ROMC (.addr(A[2:0]), .data(ROMC_data));
  ROM #(.addrWidth(3), .dataWidth(4)) ROM8 (.addr(A[2:0]), .data(ROM8_data));
  ROM #(.addrWidth(3), .dataWidth(4)) ROME (.addr(A[2:0]), .data(ROME_data));
  ROM #(.addrWidth(3), .dataWidth(4)) ROMB (.addr(A[2:0]), .data(ROMB_data));
  ROM #(.addrWidth(3), .dataWidth(4)) ROM4 (.addr(A[2:0]), .data(ROM4_data));
  ROM #(.addrWidth(3), .dataWidth(4)) ROM6 (.addr(A[2:0]), .data(ROM6_data));
  assign D = first ? {ROM0_data, ROM9_data} : 8'bz;  // Controlled_Buffer controlled_buffer_1
  assign D = second ? {ROM1_data, ROM7_data} : 8'bz;  // Controlled_Buffer controlled_buffer_2
  assign D = third ? {ROM3_data, ROMD_data} : 8'bz;  // Controlled_Buffer controlled_buffer_3
  assign D = fourth ? {ROM2_data, ROM5_data} : 8'bz;  // Controlled_Buffer controlled_buffer_4
  assign D = fifth ? {ROMF_data, ROMA_data} : 8'bz;  // Controlled_Buffer controlled_buffer_5
  assign D = sixth ? {ROM8_data, ROMC_data} : 8'bz;  // Controlled_Buffer controlled_buffer_6
  assign D = seventh ? {ROMB_data, ROME_data} : 8'bz;  // Controlled_Buffer controlled_buffer_7
  assign D = eighth ? {ROM6_data, ROM4_data} : 8'bz;  // Controlled_Buffer controlled_buffer_8

  // Other names for the same wires on the sheet: pos[2:0] = A[2:0]

  // Notes on the sheet:
  //   Attention, votre version de Logisim
  //   ne contient pas de tracker. Si vous
  //   enregistrez votre projet, toutes les
  //   informations du tracker seront
  //   définitivement effacées.
  //   contents of ROM9 (hex, n*v repeats v):
  //   3 5 4 0 1 5 9 3
  //   contents of ROM0 (hex, n*v repeats v):
  //   5 6 6 2 7 7 6 7
  //   contents of ROM7 (hex, n*v repeats v):
  //   0 3 5 3 4 f 4 9
  //   contents of ROM1 (hex, n*v repeats v):
  //   2 6 7 7 7 6 6 6
  //   contents of ROMD (hex, n*v repeats v):
  //   5 4 0 9 0 3 f 3
  //   contents of ROM3 (hex, n*v repeats v):
  //   6 7 2 6 7 7 6 7
  //   contents of ROM5 (hex, n*v repeats v):
  //   0 3 5 3 4 f 4 5
  //   contents of ROM2 (hex, n*v repeats v):
  //   2 4 7 7 7 6 6 6
  //   contents of ROMA (hex, n*v repeats v):
  //   3 f 0 8 7 8 f
  //   contents of ROMF (hex, n*v repeats v):
  //   7 3 2 2 5 6 6 2
  //   contents of ROMC (hex, n*v repeats v):
  //   7 5 1 2 4 3 0 4
  //   contents of ROM8 (hex, n*v repeats v):
  //   6 7 6 7 6 7 2 7
  //   contents of ROME (hex, n*v repeats v):
  //   8 5 0 7 5 1 2 4
  //   contents of ROMB (hex, n*v repeats v):
  //   6 6 2 4 7 6 7 6
  //   contents of ROM4 (hex, n*v repeats v):
  //   9 1 e 3 f 9 a
  //   contents of ROM6 (hex, n*v repeats v):
  //   6 6 6 7 3 2
endmodule
