// Logisim project 104418019_4.circ as structural Verilog: 4 circuits, main circuit main
module main (
  output halt,
  output [7:0] PR,
  output [3:0] ALUOUT,
  output [1:0] RT,
  output [3:0] RAMOUTPUT
);

  wire ALURAM, ALUZERO, and_1_out, and_2_out, and_3_out, CLK, or_1_out;
  wire [1:0] multiplexer_3_out, PCMODE;
  wire [2:0] ALUOP, bit_extender_1_out, multiplexer_4_out;
  wire [3:0] multiplexer_1_out, multiplexer_2_out, R1OUT, R2OUT;
  wire [7:0] ABSOLUTE;
  wire [7:7] multiplexer_5_out;
  wire [11:1] PLAOUT;
  wire [11:8] INSTRUCTION;

  Clock clock_1 (.out(CLK));
  RAM #(.addrWidth(4), .dataWidth(4), .databus("bibus")) ram_1 (
    .addr(ALUOUT), .we(PLAOUT[3]), .clk(CLK), .din(R2OUT), .dout(RAMOUTPUT));  // open: oe
  PC pc_1 (
    .CLK(CLK), .ABSOLUTE({ABSOLUTE[7:6], RT, ABSOLUTE[3:0]}), .IMMEDIATE(ABSOLUTE[3:0]), .PCMODE(PCMODE),
    .PR(PR));
  ROM #(.dataWidth(12)) rom_1 (.addr(PR), .data({INSTRUCTION, ABSOLUTE[7:6], RT, ABSOLUTE[3:0]}));
  Multiplexer #(.width(4), .enable("false")) multiplexer_1 (
    .in0(ALUOUT), .in1(RAMOUTPUT), .out(multiplexer_1_out), .sel(ALURAM));
  Multiplexer #(.width(4), .enable("false")) multiplexer_2 (
    .in0(R2OUT), .in1(ABSOLUTE[3:0]), .out(multiplexer_2_out), .sel(PLAOUT[1]));
  Multiplexer #(.width(2), .enable("false")) multiplexer_3 (
    .in0(ABSOLUTE[3:2]), .in1(RT), .out(multiplexer_3_out), .sel(PLAOUT[1]));
  ALU alu_1 (.O1IN(R1OUT), .O2IN(multiplexer_2_out), .ALUOP(ALUOP), .ALUOUT(ALUOUT), .ALUZERO(ALUZERO));
  REGFILE regfile_1 (
    .CLK(CLK), .DATAIN(multiplexer_1_out), .WENABLE(PLAOUT[9]), .WINDEX(multiplexer_3_out),
    .R1IN(ABSOLUTE[7:6]), .R2IN(RT), .R1OUT(R1OUT), .R2OUT(R2OUT));
  assign bit_extender_1_out = {{1{1'b0}}, ABSOLUTE[1:0]};  // Bit_Extender bit_extender_1
  Multiplexer #(.width(3), .enable("false")) multiplexer_4 (
    .in0(3'b000), .in1(bit_extender_1_out), .out(multiplexer_4_out), .sel(and_1_out));
  and and_1 (and_1_out, ~INSTRUCTION[11], INSTRUCTION[10], ~INSTRUCTION[9], INSTRUCTION[8]);  // AND_Gate
  Multiplexer #(.enable("false")) multiplexer_5 (.in0(1'b0), .in1(ALUZERO), .out(multiplexer_5_out[7]), .sel(or_1_out));
  or or_1 (or_1_out, and_2_out, and_3_out);
  and and_2 (and_2_out, ~INSTRUCTION[11], INSTRUCTION[10], ~INSTRUCTION[9], ~INSTRUCTION[8]);  // AND_Gate
  and and_3 (and_3_out, INSTRUCTION[11], ~INSTRUCTION[10], ~INSTRUCTION[9], INSTRUCTION[8]);  // AND_Gate
  // PLA CPUPLA: pin names not known; wires that end beside it: {multiplexer_5_out[7], INSTRUCTION, multiplexer_4_out}, {PLAOUT[11:9], ALUOP, PCMODE, PLAOUT[3], ALURAM, PLAOUT[1], halt}

  // Other names for the same wires on the sheet: OPCODE[3:0] = INSTRUCTION; EXTRA[1:0] = ABSOLUTE[1:0];
  //   IMMEDIATE[3:0] = ABSOLUTE[3:0]; INSTRUCTION[7:0] = {ABSOLUTE[7:6], RT, ABSOLUTE[3:0]}; RD[1:0] = ABSOLUTE[3:2];
  //   ABSOLUTE[5:4] = RT; RS[1:0] = ABSOLUTE[7:6]; PLAOUT (some bits) = {ALUOP, PCMODE, ALURAM, halt};
  //   RDRT = PLAOUT[1]; WRAM = PLAOUT[3]; WEN = PLAOUT[9]

  // Notes on the sheet:
  //   Attention, votre version de Logisim
  //   ne contient pas de tracker. Si vous
  //   enregistrez votre projet, toutes les
  //   informations du tracker seront
  //   définitivement effacées.
  //   contents of rom_1 (hex, n*v repeats v):
  //   811 82f 95f 56f 4bf 81b 834 c6c 8a1 d6c 821 564 57b 489 831 c6d 5ba 981 501 d6d 576 66b 988 f06
endmodule

module PC (
  input  CLK,
  input  [7:0] ABSOLUTE,
  input  [3:0] IMMEDIATE,
  input  [1:0] PCMODE,
  output [7:0] PR
);

  wire [7:0] adder_1_out, adder_2_out, bit_extender_1_out, multiplexer_1_out;

  Register #(.trigger("falling")) register_1 (.D(multiplexer_1_out), .clk(CLK), .Q(PR));  // open: en, clr
  Multiplexer #(.select(2), .width(8), .enable("false")) multiplexer_1 (
    .in0(PR), .in1(ABSOLUTE), .in2(adder_2_out), .in3(adder_1_out), .out(multiplexer_1_out), .sel(PCMODE));
  Adder adder_1 (.a(PR), .b(8'h1), .out(adder_1_out));  // open: cin, cout
  assign bit_extender_1_out = {{4{IMMEDIATE[3]}}, IMMEDIATE};  // Bit_Extender bit_extender_1
  Adder adder_2 (.a(adder_1_out), .b(bit_extender_1_out), .out(adder_2_out));  // open: cin, cout

  // Notes on the sheet:
  //   Attention, votre version de Logisim
  //   ne contient pas de tracker. Si vous
  //   enregistrez votre projet, toutes les
  //   informations du tracker seront
  //   définitivement effacées.
endmodule

module REGFILE (
  input  CLK,
  input  [3:0] DATAIN,
  input  WENABLE,
  input  [1:0] WINDEX,
  input  [1:0] R1IN,
  input  [1:0] R2IN,
  output [3:0] R1OUT,
  output [3:0] R2OUT
);

  wire decoder_1_out1, decoder_1_out2, decoder_1_out3;
  wire [3:0] R1_q, R2_q, R3_q;

  Decoder #(.select(2)) decoder_1 (
    .out1(decoder_1_out1), .out2(decoder_1_out2), .out3(decoder_1_out3), .sel(WINDEX), .en(WENABLE));  // open: out0
  Register #(.width(4), .trigger("falling")) R1 (.D(DATAIN), .en(decoder_1_out1), .clk(CLK), .Q(R1_q));  // open: clr
  Register #(.width(4), .trigger("falling")) R2 (.D(DATAIN), .en(decoder_1_out2), .clk(CLK), .Q(R2_q));  // open: clr
  Register #(.width(4), .trigger("falling")) R3 (.D(DATAIN), .en(decoder_1_out3), .clk(CLK), .Q(R3_q));  // open: clr
  Multiplexer #(.select(2), .width(4), .enable("false")) multiplexer_1 (
    .in0(4'b0000), .in1(R1_q), .in2(R2_q), .in3(R3_q), .out(R1OUT), .sel(R1IN));
  Multiplexer #(.select(2), .width(4), .enable("false")) multiplexer_2 (
    .in0(4'b0000), .in1(R1_q), .in2(R2_q), .in3(R3_q), .out(R2OUT), .sel(R2IN));

  // Notes on the sheet:
  //   Attention, votre version de Logisim
  //   ne contient pas de tracker. Si vous
  //   enregistrez votre projet, toutes les
  //   informations du tracker seront
  //   définitivement effacées.
endmodule

module ALU (
  input  [3:0] O1IN,
  input  [3:0] O2IN,
  input  [2:0] ALUOP,
  output [3:0] ALUOUT,
  output ALUZERO
);

  wire subtractor_1_bout;
  wire [3:0] adder_1_out, bit_extender_1_out, subtractor_1_out;

  Adder #(.width(4)) adder_1 (.a(O1IN), .b(O2IN), .out(adder_1_out));  // open: cin, cout
  Subtractor #(.width(4)) subtractor_1 (
    .a(O1IN), .b(O2IN), .out(subtractor_1_out), .bout(subtractor_1_bout));  // open: bin
  assign bit_extender_1_out = {{3{1'b0}}, subtractor_1_bout};  // Bit_Extender bit_extender_1
  Multiplexer #(.select(3), .width(4), .enable("false")) multiplexer_1 (
    .in0(subtractor_1_out), .in1(adder_1_out), .in6(bit_extender_1_out), .out(ALUOUT), .sel(ALUOP));  // open: in2, in3, in4, in5, in7
  Comparator #(.width(4)) comparator_1 (.a(ALUOUT), .b(4'b0000), .eq(ALUZERO));  // open: gt, lt

  // Notes on the sheet:
  //   Attention, votre version de Logisim
  //   ne contient pas de tracker. Si vous
  //   enregistrez votre projet, toutes les
  //   informations du tracker seront
  //   définitivement effacées.
endmodule
