// Logisim project 104418019_7.circ as structural Verilog: 4 circuits, main circuit PC
module main (
  output halt,
  output [11:0] PR,
  output [11:0] ALUOUT,
  output [11:0] R2OUT,
  output [11:0] RAMOUTPUT
);

  wire ALURAM, ALUZERO, CLK;
  wire [1:0] PCMODE;
  wire [2:0] ALUOP, multiplexer_2_out;
  wire [11:0] ABSOLUTE, ALU2ES, ALU2EU, bit_extender_1_out, bit_extender_2_out, counter_1_q,
       multiplexer_1_out, R1OUT;
  wire [11:1] PLAOUT;
  wire [15:12] INSTRUCTION;

  Clock clock_1 (.out(CLK));
  RAM #(.addrWidth(12), .dataWidth(12), .databus("bibus")) ram_1 (
    .addr(ALUOUT), .we(PLAOUT[3]), .clk(CLK), .din(R2OUT), .dout(RAMOUTPUT));  // open: oe
  PC pc_1 (.CLK(CLK), .ABSOLUTE(ABSOLUTE), .IMMEDIATE(ABSOLUTE[5:0]), .PCMODE(PCMODE), .PR(PR));
  ROM #(.addrWidth(12), .dataWidth(16)) rom_1 (.addr(PR), .data({INSTRUCTION, ABSOLUTE}));
  Multiplexer #(.width(12), .enable("false")) multiplexer_1 (
    .in0(ALUOUT), .in1(RAMOUTPUT), .out(multiplexer_1_out), .sel(ALURAM));
  Multiplexer #(.width(3), .enable("false")) multiplexer_2 (
    .in0(ABSOLUTE[5:3]), .in1(ABSOLUTE[8:6]), .out(multiplexer_2_out), .sel(PLAOUT[1]));
  assign bit_extender_1_out = {{6{ABSOLUTE[5]}}, ABSOLUTE[5:0]};  // Bit_Extender bit_extender_1
  assign bit_extender_2_out = {{6{1'b0}}, ABSOLUTE[5:0]};  // Bit_Extender bit_extender_2
  ALU alu_1 (.O1IN(R1OUT), .ALU2ES(ALU2ES), .ALU2EU(ALU2EU), .ALUOP(ALUOP), .ALUOUT(ALUOUT), .ALUZERO(ALUZERO));
  Multiplexer #(.width(12), .enable("false")) multiplexer_3 (
    .in0(R2OUT), .in1(bit_extender_1_out), .out(ALU2ES), .sel(PLAOUT[1]));
  Multiplexer #(.width(12), .enable("false")) multiplexer_4 (
    .in0(R2OUT), .in1(bit_extender_2_out), .out(ALU2EU), .sel(PLAOUT[1]));
  REGFILE regfile_1 (
    .CLK(CLK), .DATAIN(multiplexer_1_out), .WENABLE(PLAOUT[9]), .WINDEX(multiplexer_2_out),
    .R1IN(ABSOLUTE[11:9]), .R2IN(ABSOLUTE[8:6]), .R1OUT(R1OUT), .R2OUT(R2OUT));
  Counter #(.width(12), .max('hfff)) counter_1 (.clk(CLK), .Q(counter_1_q));  // open: clr, load, up, count, D, carry
  // PLA CPUPLA: pin names not known; wires that end beside it: {ALUZERO, INSTRUCTION, ABSOLUTE[2:0]}, {PLAOUT[11:9], ALUOP, PCMODE, PLAOUT[3], ALURAM, PLAOUT[1], halt}
  // Probe on RAMOUTPUT
  // Probe on ALUOUT
  // Probe on counter_1_q

  // Other names for the same wires on the sheet: EXTRA[2:0] = ABSOLUTE[2:0]; IMMEDIATE[5:0] = ABSOLUTE[5:0];
  //   INSTRUCTION[11:0] = ABSOLUTE; OPCODE[3:0] = INSTRUCTION; RD[2:0] = ABSOLUTE[5:3]; RT[2:0] = ABSOLUTE[8:6];
  //   RS[2:0] = ABSOLUTE[11:9]; PLAOUT (some bits) = {ALUOP, PCMODE, ALURAM, halt}; RDRT = PLAOUT[1];
  //   WRAM = PLAOUT[3]; WEN = PLAOUT[9]; RAMOUT[11:0] = RAMOUTPUT

  // Notes on the sheet:
  //   Attention, votre version de Logisim
  //   ne contient pas de tracker. Si vous
  //   enregistrez votre projet, toutes les
  //   informations du tracker seront
  //   définitivement effacées.
  //   contents of rom_1 (hex, n*v repeats v):
  //   8041 505a 31f0 3f85 51e2 c8b0 54d4 d8b0 56da 9601 80c1 8901 59ab 4377 8541 4a01 f004 7910 54f0 c950
  //   5baf d950 56da 9601 80c1 8901 6995 43b6 9a34 5001
endmodule

module PC (
  input  CLK,
  input  [11:0] ABSOLUTE,
  input  [5:0] IMMEDIATE,
  input  [1:0] PCMODE,
  output [11:0] PR
);

  wire [11:0] adder_1_out, adder_2_out, bit_extender_1_out, multiplexer_1_out;

  Register #(.width(12), .trigger("falling")) register_1 (.D(multiplexer_1_out), .clk(CLK), .Q(PR));  // open: en, clr
  Multiplexer #(.select(2), .width(12), .enable("false")) multiplexer_1 (
    .in0(PR), .in1(ABSOLUTE), .in2(adder_2_out), .in3(adder_1_out), .out(multiplexer_1_out), .sel(PCMODE));
  Adder #(.width(12)) adder_1 (.a(PR), .b(12'h1), .out(adder_1_out));  // open: cin, cout
  assign bit_extender_1_out = {{6{IMMEDIATE[5]}}, IMMEDIATE};  // Bit_Extender bit_extender_1
  Adder #(.width(12)) adder_2 (.a(adder_1_out), .b(bit_extender_1_out), .out(adder_2_out));  // open: cin, cout

  // Notes on the sheet:
  //   Attention, votre version de Logisim
  //   ne contient pas de tracker. Si vous
  //   enregistrez votre projet, toutes les
  //   informations du tracker seront
  //   définitivement effacées.
endmodule

module REGFILE (
  input  CLK,
  input  [11:0] DATAIN,
  input  WENABLE,
  input  [2:0] WINDEX,
  input  [2:0] R1IN,
  input  [2:0] R2IN,
  output [11:0] R1OUT,
  output [11:0] R2OUT
);

  wire decoder_1_out1, decoder_1_out2, decoder_1_out3, decoder_1_out4, decoder_1_out5, decoder_1_out6,
       decoder_1_out7;
  wire [11:0] R1_q, R2_q, R3_q, R4_q, R5_q, R6_q, R7_q;

  Decoder #(.select(3)) decoder_1 (
    .out1(decoder_1_out1), .out2(decoder_1_out2), .out3(decoder_1_out3), .out4(decoder_1_out4),
    .out5(decoder_1_out5), .out6(decoder_1_out6), .out7(decoder_1_out7), .sel(WINDEX), .en(WENABLE));  // open: out0
  Register #(.width(12), .trigger("falling")) R1 (.D(DATAIN), .en(decoder_1_out1), .clk(CLK), .Q(R1_q));  // open: clr
  Register #(.width(12), .trigger("falling")) R2 (.D(DATAIN), .en(decoder_1_out2), .clk(CLK), .Q(R2_q));  // open: clr
  Register #(.width(12), .trigger("falling")) R3 (.D(DATAIN), .en(decoder_1_out3), .clk(CLK), .Q(R3_q));  // open: clr
  Register #(.width(12), .trigger("falling")) R4 (.D(DATAIN), .en(decoder_1_out4), .clk(CLK), .Q(R4_q));  // open: clr
  Register #(.width(12), .trigger("falling")) R5 (.D(DATAIN), .en(decoder_1_out5), .clk(CLK), .Q(R5_q));  // open: clr
  Register #(.width(12), .trigger("falling")) R6 (.D(DATAIN), .en(decoder_1_out6), .clk(CLK), .Q(R6_q));  // open: clr
  Register #(.width(12), .trigger("falling")) R7 (.D(DATAIN), .en(decoder_1_out7), .clk(CLK), .Q(R7_q));  // open: clr
  Multiplexer #(.select(3), .width(12), .enable("false")) multiplexer_1 (
    .in0({12{1'b0}}), .in1(R1_q), .in2(R2_q), .in3(R3_q), .in4(R4_q), .in5(R5_q), .in6(R6_q), .in7(R7_q),
    .out(R1OUT), .sel(R1IN));
  Multiplexer #(.select(3), .width(12), .enable("false")) multiplexer_2 (
    .in0({12{1'b0}}), .in1(R1_q), .in2(R2_q), .in3(R3_q), .in4(R4_q), .in5(R5_q), .in6(R6_q), .in7(R7_q),
    .out(R2OUT), .sel(R2IN));

  // Notes on the sheet:
  //   Attention, votre version de Logisim
  //   ne contient pas de tracker. Si vous
  //   enregistrez votre projet, toutes les
  //   informations du tracker seront
  //   définitivement effacées.
endmodule

module ALU (
  input  [11:0] O1IN,
  input  [11:0] ALU2ES,
  input  [11:0] ALU2EU,
  input  [2:0] ALUOP,
  output [11:0] ALUOUT,
  output ALUZERO
);

  wire subtractor_1_bout;
  wire [11:0] adder_1_out, and_1_out, bit_extender_1_out, or_1_out, subtractor_1_out;

  Adder #(.width(12)) adder_1 (.a(O1IN), .b(ALU2ES), .out(adder_1_out));  // open: cin, cout
  Subtractor #(.width(12)) subtractor_1 (
    .a(O1IN), .b(ALU2ES), .out(subtractor_1_out), .bout(subtractor_1_bout));  // open: bin
  assign bit_extender_1_out = {{11{1'b0}}, subtractor_1_bout};  // Bit_Extender bit_extender_1
  assign or_1_out = O1IN | ALU2EU;  // OR_Gate or_1, 12 bits wide
  assign and_1_out = O1IN & ALU2EU;  // AND_Gate and_1, 12 bits wide
  Multiplexer #(.select(3), .width(12), .enable("false")) multiplexer_1 (
    .in0(subtractor_1_out), .in1(adder_1_out), .in3(or_1_out), .in5(and_1_out), .in6(bit_extender_1_out),
    .out(ALUOUT), .sel(ALUOP));  // open: in2, in4, in7
  Comparator #(.width(12)) comparator_1 (.a(ALUOUT), .b({12{1'b0}}), .eq(ALUZERO));  // open: gt, lt

  // Notes on the sheet:
  //   Attention, votre version de Logisim
  //   ne contient pas de tracker. Si vous
  //   enregistrez votre projet, toutes les
  //   informations du tracker seront
  //   définitivement effacées.
endmodule
